// Logisim project ComputerTest.circ as structural Verilog: 8 circuits, main circuit main
module main (
  input  [25:0] Address,
  input  [31:0] Data,
  input  [2:0] func3,
  output [31:0] LoadData
);

  wire clock_1_out, dipswitch_1_sw1, dipswitch_1_sw2, not_1_out;
  wire [31:0] ram_1_dout, ram_setter_1_bytestore, transistor_1_out;

  DipSwitch #(.number(2)) dipswitch_1 (.sw1(dipswitch_1_sw1), .sw2(dipswitch_1_sw2));
  Clock clock_1 (.out(clock_1_out));
  not not_1 (not_1_out, 1'b1);
  RAM #(.addrWidth(24), .dataWidth(32)) ram_1 (
    .addr(Address[25:2]), .we(dipswitch_1_sw2), .oe(1'b1), .clk(clock_1_out), .din(ram_setter_1_bytestore),
    .dout(ram_1_dout));
  Transistor #(.width(32)) transistor_1 (.in(Data), .out(transistor_1_out), .gate(not_1_out));
  RAM_SETTER ram_setter_1 (
    .DATA(transistor_1_out), .MEMORY(ram_1_dout), .FUNC3(func3), .BYTELOCATION(Address[1:0]),
    .LOAD(dipswitch_1_sw1), .ByteStore(ram_setter_1_bytestore), .ByteLoad(LoadData));

  // Notes on the sheet:
  //   Load
  //   Store
endmodule

module ALU (
  input  [6:0] func7,
  input  [31:0] rs1,
  input  [31:0] rs2,
  input  [2:0] func3,
  input  [31:0] imm_value,
  input  immediate,
  input  is_active,
  output [31:0] rd
);

  wire and_2_out, comparator_1_gt, comparator_2_gt, not_1_out;
  wire [4:0] multiplexer_1_out;
  wire [31:0] adder_1_out, and_1_out, bit_extender_1_out, bit_extender_2_out, multiplexer_2_out,
       multiplexer_3_out, multiplexer_4_out, or_1_out, shifter_1_out, shifter_2_out, shifter_3_out,
       subtractor_1_out, xor_1_out;
  wire [31:5] multiplexer_1_out_2;

  Multiplexer #(.width(32)) multiplexer_1 (
    .in0(rs2), .in1(imm_value), .out({multiplexer_1_out_2, multiplexer_1_out}), .sel(immediate));
  not not_1 (not_1_out, immediate);
  Adder #(.width(32)) adder_1 (
    .a(rs1), .b({multiplexer_1_out_2, multiplexer_1_out}), .out(adder_1_out));  // open: cin, cout
  Subtractor #(.width(32)) subtractor_1 (
    .a(rs1), .b({multiplexer_1_out_2, multiplexer_1_out}), .out(subtractor_1_out));  // open: bin, bout
  Shifter #(.width(32)) shifter_1 (
    .in({multiplexer_1_out_2, multiplexer_1_out}), .\dist (multiplexer_1_out), .out(shifter_1_out));
  Comparator #(.width(32)) comparator_1 (
    .a(rs1), .b({multiplexer_1_out_2, multiplexer_1_out}), .gt(comparator_1_gt));  // open: eq, lt
  Comparator #(.mode("unsigned"), .width(32)) comparator_2 (
    .a({multiplexer_1_out_2, multiplexer_1_out}), .b({multiplexer_1_out_2, multiplexer_1_out}),
    .gt(comparator_2_gt));  // open: eq, lt
  assign xor_1_out = rs1 ^ {multiplexer_1_out_2, multiplexer_1_out};  // XOR_Gate xor_1, 32 bits wide
  Shifter #(.shift("lr"), .width(32)) shifter_2 (.in(rs1), .\dist (multiplexer_1_out), .out(shifter_2_out));
  Shifter #(.shift("ar"), .width(32)) shifter_3 (.in(rs1), .\dist (multiplexer_1_out), .out(shifter_3_out));
  assign bit_extender_1_out = {{31{comparator_1_gt}}, comparator_1_gt};  // Bit_Extender bit_extender_1
  assign bit_extender_2_out = {{31{comparator_2_gt}}, comparator_2_gt};  // Bit_Extender bit_extender_2
  assign or_1_out = rs1 | {multiplexer_1_out_2, multiplexer_1_out};  // OR_Gate or_1, 32 bits wide
  assign and_1_out = rs1 & {multiplexer_1_out_2, multiplexer_1_out};  // AND_Gate and_1, 32 bits wide
  Multiplexer #(.width(32)) multiplexer_2 (
    .in0(adder_1_out), .in1(subtractor_1_out), .out(multiplexer_2_out), .sel(and_2_out));
  Multiplexer #(.width(32)) multiplexer_3 (
    .in0(shifter_2_out), .in1(shifter_3_out), .out(multiplexer_3_out), .sel(and_2_out));
  and and_2 (and_2_out, func7[5], not_1_out);
  Multiplexer #(.select(3), .width(32)) multiplexer_4 (
    .in0(multiplexer_2_out), .in1(shifter_1_out), .in2(bit_extender_1_out), .in3(bit_extender_2_out),
    .in4(xor_1_out), .in5(multiplexer_3_out), .in6(or_1_out), .in7(and_1_out), .out(multiplexer_4_out),
    .sel(func3));
  assign rd = is_active ? multiplexer_4_out : 32'bz;  // Controlled_Buffer controlled_buffer_1
endmodule

module RAM_SETTER (
  input  [31:0] DATA,
  input  [31:0] MEMORY,
  input  [2:0] FUNC3,
  input  [1:0] BYTELOCATION,
  input  LOAD,
  output [31:0] ByteStore,
  output [31:0] ByteLoad
);

  wire [7:0] multiplexer_3_out;
  wire [15:0] multiplexer_4_out;
  wire [31:0] bit_extender_1_out, bit_extender_2_out, bit_extender_3_out, multiplexer_1_out,
       multiplexer_2_out, multiplexer_5_out, multiplexer_6_out;

  assign bit_extender_1_out = {{31{LOAD}}, LOAD};  // Bit_Extender bit_extender_1
  Multiplexer #(.width(32)) multiplexer_1 (
    .in0({MEMORY[31:16], DATA[15:0]}), .in1({DATA[15:0], MEMORY[15:0]}), .out(multiplexer_1_out),
    .sel(BYTELOCATION[1]));
  Multiplexer #(.select(2), .width(32)) multiplexer_2 (
    .in0({MEMORY[31:8], DATA[7:0]}), .in1({MEMORY[31:16], DATA[7:0], MEMORY[7:0]}),
    .in2({MEMORY[31:24], DATA[7:0], MEMORY[15:0]}), .in3({DATA[7:0], MEMORY[23:0]}), .out(multiplexer_2_out),
    .sel(BYTELOCATION));
  Multiplexer #(.select(2), .width(8)) multiplexer_3 (
    .in0(MEMORY[7:0]), .in1(MEMORY[15:8]), .in2(MEMORY[23:16]), .in3(MEMORY[31:24]), .out(multiplexer_3_out),
    .sel(BYTELOCATION));
  Multiplexer #(.width(16)) multiplexer_4 (
    .in0(MEMORY[15:0]), .in1(MEMORY[31:16]), .out(multiplexer_4_out), .sel(BYTELOCATION[1]));
  assign bit_extender_2_out = {{24{multiplexer_3_out[7]}}, multiplexer_3_out};  // Bit_Extender bit_extender_2
  assign bit_extender_3_out = {{16{multiplexer_4_out[15]}}, multiplexer_4_out};  // Bit_Extender bit_extender_3
  Multiplexer #(.select(3), .width(32)) multiplexer_5 (
    .in0(multiplexer_2_out), .in1(multiplexer_1_out), .in2(DATA), .out(multiplexer_5_out), .sel(FUNC3));  // open: in3, in4, in5, in6, in7
  assign ByteStore = {32{1'b0}} | multiplexer_5_out;  // OR_Gate or_1, 32 bits wide
  Multiplexer #(.select(3), .width(32)) multiplexer_6 (
    .in0(bit_extender_2_out), .in1(bit_extender_3_out), .in2(MEMORY), .out(multiplexer_6_out), .sel(FUNC3));  // open: in3, in4, in5, in6, in7
  assign ByteLoad = multiplexer_6_out & bit_extender_1_out;  // AND_Gate and_1, 32 bits wide
endmodule

module bigtransistor (
  input  Gate,
  input  [31:0] Source,
  output [31:0] Drain
);

  wire not_1_out;
  wire [31:0] and_1_out, bit_extender_1_out;

  assign bit_extender_1_out = {{31{Gate}}, Gate};  // Bit_Extender bit_extender_1
  not not_1 (not_1_out, Gate);
  assign and_1_out = bit_extender_1_out & Source;  // AND_Gate and_1, 32 bits wide
  Multiplexer #(.width(32)) multiplexer_1 (.in0(and_1_out), .out(Drain), .sel(not_1_out));  // open: in1
endmodule

module cpu (
);

  wire bus_decoder_1_branch, bus_decoder_1_clockload, bus_decoder_1_is_imm, bus_decoder_1_load,
       bus_decoder_1_store, condition_evaluator_1_result;
  wire [2:0] bus_decoder_1_func3;
  wire [4:0] bus_decoder_1_rd, bus_decoder_1_rs1, bus_decoder_1_rs2;
  wire [6:0] bus_decoder_1_func7;
  wire [31:0] alu_1_rd, bus_decoder_1_imm, registers_v2_1_pc, registers_v2_1_rs1out, registers_v2_1_rs2out;

  ROM #(.addrWidth(24), .dataWidth(32)) rom_1 (.addr(registers_v2_1_pc[23:0]));  // open: data
  bus_decoder bus_decoder_1 (
    .func3(bus_decoder_1_func3), .func7(bus_decoder_1_func7), .rs1(bus_decoder_1_rs1),
    .rs2(bus_decoder_1_rs2), .rd(bus_decoder_1_rd), .imm(bus_decoder_1_imm), .is_imm(bus_decoder_1_is_imm),
    .branch(bus_decoder_1_branch), .store(bus_decoder_1_store), .load(bus_decoder_1_load),
    .clockload(bus_decoder_1_clockload));
  registers_v2 registers_v2_1 (
    .data(alu_1_rd), .rs1(bus_decoder_1_rs1), .rs2(bus_decoder_1_rs2), .rd(bus_decoder_1_rd),
    .store(bus_decoder_1_store), .load(bus_decoder_1_load), .clock(bus_decoder_1_clockload),
    .jump(condition_evaluator_1_result), .rs1out(registers_v2_1_rs1out), .rs2out(registers_v2_1_rs2out),
    .pc(registers_v2_1_pc));
  ALU alu_1 (
    .func7(bus_decoder_1_func7), .rs1(registers_v2_1_rs1out), .rs2(registers_v2_1_rs2out),
    .func3(bus_decoder_1_func3), .imm_value(bus_decoder_1_imm), .immediate(bus_decoder_1_is_imm),
    .rd(alu_1_rd));  // open: is_active
  condition_evaluator condition_evaluator_1 (
    .rs1(registers_v2_1_rs1out), .rs2(registers_v2_1_rs2out), .func3(bus_decoder_1_func3),
    .result(condition_evaluator_1_result));  // open: is_active
endmodule

module condition_evaluator (
  input  [31:0] rs1,
  input  [31:0] rs2,
  input  [2:0] func3,
  input  is_active,
  output result
);

  wire comparator_1_eq, comparator_1_gt, comparator_1_lt, comparator_2_eq, comparator_2_gt, comparator_2_lt,
       multiplexer_1_out, not_1_out, or_1_out, or_2_out;

  Comparator #(.width(32)) comparator_1 (
    .a(rs1), .b(rs2), .gt(comparator_1_gt), .eq(comparator_1_eq), .lt(comparator_1_lt));
  Comparator #(.mode("unsigned"), .width(32)) comparator_2 (
    .a(rs1), .b(rs2), .gt(comparator_2_gt), .eq(comparator_2_eq), .lt(comparator_2_lt));
  or or_1 (or_1_out, comparator_1_gt, comparator_1_eq);
  or or_2 (or_2_out, comparator_2_gt, comparator_2_eq);
  not not_1 (not_1_out, comparator_1_eq);
  Multiplexer #(.select(3)) multiplexer_1 (
    .in0(comparator_1_eq), .in1(not_1_out), .in4(comparator_1_lt), .in5(or_1_out), .in6(comparator_2_lt),
    .in7(or_2_out), .out(multiplexer_1_out), .sel(func3));  // open: in2, in3
  assign result = is_active ? multiplexer_1_out : 1'bz;  // Controlled_Buffer controlled_buffer_1
endmodule

module registers_v2 (
  input  [31:0] data,
  input  [4:0] rs1,
  input  [4:0] rs2,
  input  [4:0] rd,
  input  store,
  input  load,
  input  clock,
  input  jump,
  output [31:0] rs1out,
  output [31:0] rs2out,
  output [31:0] pc
);

  wire and_1_out, and_2_out, and_3_out, and_4_out, and_5_out, and_6_out, and_7_out, and_8_out, d_ff_1_q,
       nor_1_out, nor_2_out, nor_3_out, nor_4_out, not_1_out;
  wire [4:0] multiplexer_1_out, multiplexer_2_out;
  wire [31:0] ram_1_dout, ram_2_dout, register_1_q;

  and and_1 (and_1_out, rs1[0], rs1[1], rs1[2], rs1[3], rs1[4], and_6_out);
  nor nor_1 (nor_1_out, rs1[0], rs1[1], rs1[2], rs1[3], rs1[4]);
  nor nor_2 (nor_2_out, rs2[0], rs2[1], rs2[2], rs2[3], rs2[4]);
  and and_2 (and_2_out, rs2[0], rs2[1], rs2[2], rs2[3], rs2[4], and_6_out);
  and and_3 (and_3_out, and_6_out, nor_1_out);
  D_Flip_Flop d_ff_1 (.D(store), .clk(not_1_out), .Q(d_ff_1_q));  // open: Qn, preset, reset
  and and_4 (and_4_out, and_6_out, nor_2_out);
  Register #(.width(32)) register_1 (.D(data), .en(not_1_out), .clk(not_1_out), .Q(register_1_q));  // open: clr
  and and_5 (and_5_out, d_ff_1_q, not_1_out);
  and and_6 (and_6_out, load, clock);
  not not_1 (not_1_out, clock);
  RAM #(.addrWidth(5), .dataWidth(32), .trigger("high")) ram_1 (
    .addr(multiplexer_1_out), .we(and_5_out), .oe(and_6_out), .din(register_1_q), .dout(ram_1_dout));
  Multiplexer #(.width(5)) multiplexer_1 (.in0(rs1), .in1(rd), .out(multiplexer_1_out), .sel(not_1_out));
  RAM #(.addrWidth(5), .dataWidth(32), .trigger("high")) ram_2 (
    .addr(multiplexer_2_out), .we(and_5_out), .oe(and_6_out), .din(register_1_q), .dout(ram_2_dout));
  Multiplexer #(.width(5)) multiplexer_2 (.in0(rs2), .in1(rd), .out(multiplexer_2_out), .sel(not_1_out));
  nor nor_3 (nor_3_out, and_4_out, and_2_out);
  Counter #(.max('hffffffff), .width(32)) counter_1 (
    .load(jump), .D(register_1_q), .Q(pc), .clk(clock));  // open: count, carry, up, clr
  nor nor_4 (nor_4_out, and_1_out, and_3_out);
  assign rs1out = and_8_out ? ram_1_dout : 32'bz;  // Controlled_Buffer controlled_buffer_1
  assign rs2out = and_7_out ? ram_2_dout : 32'bz;  // Controlled_Buffer controlled_buffer_2
  and and_7 (and_7_out, nor_3_out, and_6_out);
  assign rs1out = and_3_out ? {32{1'b0}} : 32'bz;  // Controlled_Buffer controlled_buffer_3
  assign rs1out = and_1_out ? pc : 32'bz;  // Controlled_Buffer controlled_buffer_4
  and and_8 (and_8_out, nor_4_out, and_6_out);
  assign rs2out = and_2_out ? pc : 32'bz;  // Controlled_Buffer controlled_buffer_5
  assign rs2out = and_4_out ? {32{1'b0}} : 32'bz;  // Controlled_Buffer controlled_buffer_6
endmodule

module bus_decoder (
  output [2:0] func3,
  output [6:0] func7,
  output [4:0] rs1,
  output [4:0] rs2,
  output [4:0] rd,
  output [31:0] imm,
  output is_imm,
  output branch,
  output store,
  output load,
  output clockload
);

  Clock clock_1 (.out(clockload));
endmodule
